// Logisim project sequential-logic.circ as structural Verilog
module rs_latch (
  input  r,
  input  s,
  output out,
  output not_out
);

  \nor  nor_1 (.a(r), .b(not_out), .out(out));
  \nor  nor_2 (.a(out), .b(s), .out(not_out));
endmodule

module d_latch (
  input  in,
  input  load,
  output out,
  output not_out
);

  wire and_1_out, and_2_out, not_1_output;

  \not  not_1 (.\input (in), .\output (not_1_output));
  \and  and_1 (.a(not_1_output), .b(load), .out(and_1_out));
  \and  and_2 (.a(in), .b(load), .out(and_2_out));
  rs_latch rs_latch_1 (.r(and_1_out), .s(and_2_out), .out(out), .not_out(not_out));

  // Notes on the sheet:
  //   reset
  //   set
endmodule

module d_latch_tmp (
  input  in_1,
  input  in_2,
  output out_3
);

  wire and_1_out, and_2_out, not_1_output;

  \not  not_1 (.\input (in_2), .\output (not_1_output));
  \and  and_1 (.a(in_1), .b(in_2), .out(and_1_out));
  \and  and_2 (.a(not_1_output), .b(out_3), .out(and_2_out));
  \or  or_1 (.a(and_1_out), .b(and_2_out), .out(out_3));
endmodule

module _8_bit_reg (
  input  clk,
  input  load,
  input  [7:0] in,
  output [7:0] out_4
);

  wire and_1_out;

  \and  and_1 (.a(clk), .b(load), .out(and_1_out));
  d_latch d_latch_1 (.in(in[0]), .load(and_1_out), .out(out_4[0]));  // open: not_out
  d_latch d_latch_2 (.in(in[1]), .load(and_1_out), .out(out_4[1]));  // open: not_out
  d_latch d_latch_3 (.in(in[2]), .load(and_1_out), .out(out_4[2]));  // open: not_out
  d_latch d_latch_4 (.in(in[3]), .load(and_1_out), .out(out_4[3]));  // open: not_out
  d_latch d_latch_5 (.in(in[4]), .load(and_1_out), .out(out_4[4]));  // open: not_out
  d_latch d_latch_6 (.in(in[5]), .load(and_1_out), .out(out_4[5]));  // open: not_out
  d_latch d_latch_7 (.in(in[6]), .load(and_1_out), .out(out_4[6]));  // open: not_out
  d_latch d_latch_8 (.in(in[7]), .load(and_1_out), .out(out_4[7]));  // open: not_out
endmodule
